# Fritzing sketch file 19 (saved by Fritzing 0.9.4)
breadboards: 1

parts:
  Part1 = Arduino Uno (Rev3)
  HC-SR04_Sensor_1 = HC-SR04 Ultrasonic Distance Sensor
  LED1 = smd LED [color="Red (633nm)" package="1206 [SMD]"]
  R1 = Resistor [tolerance=±5% resistance=220 package=THT]

nets:
  N1: Part1.D11_PWM/MOSI, HC-SR04_Sensor_1.TRIG
  N2: Part1.D12/MISO, HC-SR04_Sensor_1.ECHO
  N3: Part1.D3_PWM, LED1.anode
  5V: Part1.5V, HC-SR04_Sensor_1.VCC
  GND: Part1.GND, HC-SR04_Sensor_1.GND, R1.Pin_0
  N4: LED1.cathode, R1.Pin_1
